// Logisim project P0_L0_CRC.circ as structural Verilog: 3 circuits, main circuit CRC
module CRC (
  input  [7:0] in_1,
  input  [3:0] B,
  output [10:0] out_3
);

  wire [2:0] n4bit_1_remainder, n4bit_2_remainder, n4bit_3_remainder, n4bit_4_remainder, n4bit_5_remainder,
       n4bit_6_remainder, n4bit_7_remainder;
  wire [3:0] shifter_1_out_2;
  wire [6:0] shifter_1_out;
  wire [10:0] bit_extender_1_out;

  assign bit_extender_1_out = {{3{1'b0}}, in_1};  // Bit_Extender bit_extender_1
  // Probe on {shifter_1_out_2, shifter_1_out}
  Shifter #(.width(11)) shifter_1 (.in(bit_extender_1_out), .\dist (4'b0011), .out({shifter_1_out_2, shifter_1_out}));
  _4bit u_4bit_1 (.dividend(shifter_1_out_2), .divider(B), .remainder(n4bit_1_remainder));
  _4bit u_4bit_2 (.dividend({n4bit_1_remainder, shifter_1_out[6]}), .divider(B), .remainder(n4bit_2_remainder));
  _4bit u_4bit_3 (.dividend({n4bit_2_remainder, shifter_1_out[5]}), .divider(B), .remainder(n4bit_3_remainder));
  _4bit u_4bit_4 (.dividend({n4bit_3_remainder, shifter_1_out[4]}), .divider(B), .remainder(n4bit_4_remainder));
  _4bit u_4bit_5 (.dividend({n4bit_4_remainder, shifter_1_out[3]}), .divider(B), .remainder(n4bit_5_remainder));
  _4bit u_4bit_6 (.dividend({n4bit_5_remainder, shifter_1_out[2]}), .divider(B), .remainder(n4bit_6_remainder));
  _4bit u_4bit_7 (.dividend({n4bit_6_remainder, shifter_1_out[1]}), .divider(B), .remainder(n4bit_7_remainder));
  _4bit u_4bit_8 (.dividend({n4bit_7_remainder, shifter_1_out[0]}), .divider(B), .remainder(out_3[2:0]));

  assign out_3[10:3] = in_1;
endmodule

module _4bit (
  input  [3:0] dividend,
  input  [3:0] divider,
  output [2:0] remainder
);

  wire [3:0] xor_1_out;
  wire [3:3] multiplexer_1_out;

  assign xor_1_out = dividend ^ divider;  // XOR_Gate xor_1, 4 bits wide
  Multiplexer #(.width(4)) multiplexer_1 (
    .in0(dividend), .in1(xor_1_out), .out({multiplexer_1_out[3], remainder}), .sel(dividend[3]));  // open: en

  // Notes on the sheet:
  //   保证首位为1，每次得到首位为0再开始计算
  //   没有那么简单，不要太想当然，人做除法当然可以判断首位是否为0，但是这对机器很难。
  //   有这个判断，还不如直接从头除到位更划算
endmodule

module teest (
  output out_1
);

  wire clock_1_out;
  wire [7:0] counter_1_q;

  Counter counter_1 (.Q(counter_1_q), .carry(out_1), .clk(clock_1_out));  // open: load, D, count, clr
  Clock clock_1 (.out(clock_1_out));
  ROM #(.dataWidth(12)) rom_1 (.addr(counter_1_q));  // open: data, sel

  // Notes on the sheet:
  //   contents of rom_1 (hex, n*v repeats v):
  //   fff
endmodule
