// Logisim project P0_L0_FSM.circ as structural Verilog: 3 circuits, main circuit fsm
module \状态转移  (
  input  s1,
  input  s0,
  input  in1,
  input  in0,
  output s1_2,
  output s0_2
);

  wire and_1_out, and_2_out, and_3_out, and_4_out, and_5_out, and_6_out, and_7_out, not_1_out, not_2_out,
       not_3_out, not_4_out, not_5_out, not_6_out, not_7_out;

  not not_1 (not_1_out, s1);
  and and_1 (and_1_out, not_1_out, s0);
  not not_2 (not_2_out, in0);
  and and_2 (and_2_out, s1, not_3_out);
  not not_3 (not_3_out, s0);
  not not_4 (not_4_out, in0);
  not not_5 (not_5_out, in1);
  and and_3 (and_3_out, s1, not_6_out);
  not not_6 (not_6_out, s0);
  not not_7 (not_7_out, in0);
  and and_4 (and_4_out, and_1_out, not_2_out);
  and and_5 (and_5_out, and_2_out, not_4_out);
  and and_6 (and_6_out, not_5_out, in0);
  and and_7 (and_7_out, and_3_out, not_7_out);
  or or_1 (s1_2, and_4_out, and_5_out);
  or or_2 (s0_2, and_6_out, and_7_out);
endmodule

module \输出逻辑  (
  input  s1,
  input  s0,
  input  in1,
  input  in0,
  output fsm
);

  wire and_1_out, not_1_out, not_2_out;

  and and_1 (and_1_out, s1, not_1_out);
  not not_1 (not_1_out, s0);
  not not_2 (not_2_out, in0);
  and and_2 (fsm, and_1_out, not_2_out);
endmodule

module fsm (
  input  in_1,
  input  [1:0] IN,
  output out_3
);

  wire CLK;
  wire [1:0] in_t, multiplexer_1_out, state_q, \状态转移_1_s0_2 ;

  Clock clock_1 (.out(CLK));
  \状态转移  \u_状态转移_1  (
    .s1(state_q[1]), .s0(state_q[0]), .s1_2(\状态转移_1_s0_2 [1]), .in1(IN[1]), .in0(IN[0]),
    .s0_2(\状态转移_1_s0_2 [0]));
  Multiplexer #(.width(2), .disabled(0), .enable("false")) multiplexer_1 (
    .in0(\状态转移_1_s0_2 ), .in1(2'b00), .out(multiplexer_1_out), .sel(in_1));
  Register #(.width(2)) state (.D(multiplexer_1_out), .Q(state_q), .clk(CLK));  // open: en, clr
  Register #(.width(2)) u_in (.Q(in_t), .clk(CLK), .clr(in_1));  // open: D, en
  \输出逻辑  \u_输出逻辑_1  (.s1(state_q[1]), .fsm(out_3), .s0(state_q[0]), .in1(IN[1]), .in0(IN[0]));

  // Other names for the same wires on the sheet: reset = in_1
endmodule
