// Logisim project P0_L0_GRF.circ as structural Verilog: 1 circuit, main circuit grf
module grf (
  input  reset,
  input  WE,
  input  clk,
  input  [4:0] in_4,
  input  [4:0] in_5,
  input  [4:0] A3,
  input  [31:0] WD,
  output [31:0] RD1,
  output [31:0] RD2
);

  wire decoder_1_out0, decoder_1_out1, decoder_1_out2, decoder_1_out3, decoder_1_out4, decoder_1_out5,
       decoder_1_out6, decoder_1_out7, decoder_1_out8, decoder_1_out9, decoder_1_out10, decoder_1_out11,
       decoder_1_out12, decoder_1_out13, decoder_1_out14, decoder_1_out15, decoder_1_out16, decoder_1_out17,
       decoder_1_out18, decoder_1_out19, decoder_1_out20, decoder_1_out21, decoder_1_out22, decoder_1_out23,
       decoder_1_out24, decoder_1_out25, decoder_1_out26, decoder_1_out27, decoder_1_out28, decoder_1_out29,
       decoder_1_out30, decoder_1_out31;
  wire [31:0] _0, _1, _2, _3, _4, _5, _6, _7, _8, _9, _10, _11, _12, _13, _14, _15, _16, _17, _18, _19, _20,
       _21, _22, _23, _24, _25, _26, _27, _28, _29, _30, _31;

  Decoder #(.select(5), .disabled(0)) decoder_1 (
    .out0(decoder_1_out0), .out1(decoder_1_out1), .out2(decoder_1_out2), .out3(decoder_1_out3),
    .out4(decoder_1_out4), .out5(decoder_1_out5), .out6(decoder_1_out6), .out7(decoder_1_out7),
    .out8(decoder_1_out8), .out9(decoder_1_out9), .out10(decoder_1_out10), .out11(decoder_1_out11),
    .out12(decoder_1_out12), .out13(decoder_1_out13), .out14(decoder_1_out14), .out15(decoder_1_out15),
    .out16(decoder_1_out16), .out17(decoder_1_out17), .out18(decoder_1_out18), .out19(decoder_1_out19),
    .out20(decoder_1_out20), .out21(decoder_1_out21), .out22(decoder_1_out22), .out23(decoder_1_out23),
    .out24(decoder_1_out24), .out25(decoder_1_out25), .out26(decoder_1_out26), .out27(decoder_1_out27),
    .out28(decoder_1_out28), .out29(decoder_1_out29), .out30(decoder_1_out30), .out31(decoder_1_out31),
    .sel(A3), .en(WE));
  Register #(.width(32)) u__0 (.D({32{1'b0}}), .en(decoder_1_out0), .Q(_0), .clk(clk), .clr(reset));
  Register #(.width(32)) u__8 (.D(WD), .en(decoder_1_out8), .Q(_8), .clk(clk), .clr(reset));
  Register #(.width(32)) u__16 (.D(WD), .en(decoder_1_out16), .Q(_16), .clk(clk), .clr(reset));
  Register #(.width(32)) u__24 (.D(WD), .en(decoder_1_out24), .Q(_24), .clk(clk), .clr(reset));
  Register #(.width(32)) u__1 (.D(WD), .en(decoder_1_out1), .Q(_1), .clk(clk), .clr(reset));
  Register #(.width(32)) u__9 (.D(WD), .en(decoder_1_out9), .Q(_9), .clk(clk), .clr(reset));
  Register #(.width(32)) u__17 (.D(WD), .en(decoder_1_out17), .Q(_17), .clk(clk), .clr(reset));
  Register #(.width(32)) u__25 (.D(WD), .en(decoder_1_out25), .Q(_25), .clk(clk), .clr(reset));
  Register #(.width(32)) u__2 (.D(WD), .en(decoder_1_out2), .Q(_2), .clk(clk), .clr(reset));
  Register #(.width(32)) u__10 (.D(WD), .en(decoder_1_out10), .Q(_10), .clk(clk), .clr(reset));
  Register #(.width(32)) u__18 (.D(WD), .en(decoder_1_out18), .Q(_18), .clk(clk), .clr(reset));
  Register #(.width(32)) u__26 (.D(WD), .en(decoder_1_out26), .Q(_26), .clk(clk), .clr(reset));
  Register #(.width(32)) u__3 (.D(WD), .en(decoder_1_out3), .Q(_3), .clk(clk), .clr(reset));
  Register #(.width(32)) u__11 (.D(WD), .en(decoder_1_out11), .Q(_11), .clk(clk), .clr(reset));
  Register #(.width(32)) u__19 (.D(WD), .en(decoder_1_out19), .Q(_19), .clk(clk), .clr(reset));
  Register #(.width(32)) u__27 (.D(WD), .en(decoder_1_out27), .Q(_27), .clk(clk), .clr(reset));
  Register #(.width(32)) u__4 (.D(WD), .en(decoder_1_out4), .Q(_4), .clk(clk), .clr(reset));
  Register #(.width(32)) u__12 (.D(WD), .en(decoder_1_out12), .Q(_12), .clk(clk), .clr(reset));
  Register #(.width(32)) u__20 (.D(WD), .en(decoder_1_out20), .Q(_20), .clk(clk), .clr(reset));
  Register #(.width(32)) u__28 (.D(WD), .en(decoder_1_out28), .Q(_28), .clk(clk), .clr(reset));
  Register #(.width(32)) u__5 (.D(WD), .en(decoder_1_out5), .Q(_5), .clk(clk), .clr(reset));
  Register #(.width(32)) u__13 (.D(WD), .en(decoder_1_out13), .Q(_13), .clk(clk), .clr(reset));
  Register #(.width(32)) u__21 (.D(WD), .en(decoder_1_out21), .Q(_21), .clk(clk), .clr(reset));
  Register #(.width(32)) u__29 (.D(WD), .en(decoder_1_out29), .Q(_29), .clk(clk), .clr(reset));
  Register #(.width(32)) u__6 (.D(WD), .en(decoder_1_out6), .Q(_6), .clk(clk), .clr(reset));
  Register #(.width(32)) u__14 (.D(WD), .en(decoder_1_out14), .Q(_14), .clk(clk), .clr(reset));
  Register #(.width(32)) u__22 (.D(WD), .en(decoder_1_out22), .Q(_22), .clk(clk), .clr(reset));
  Register #(.width(32)) u__30 (.D(WD), .en(decoder_1_out30), .Q(_30), .clk(clk), .clr(reset));
  Register #(.width(32)) u__7 (.D(WD), .en(decoder_1_out7), .Q(_7), .clk(clk), .clr(reset));
  Register #(.width(32)) u__15 (.D(WD), .en(decoder_1_out15), .Q(_15), .clk(clk), .clr(reset));
  Register #(.width(32)) u__23 (.D(WD), .en(decoder_1_out23), .Q(_23), .clk(clk), .clr(reset));
  Register #(.width(32)) u__31 (.D(WD), .en(decoder_1_out31), .Q(_31), .clk(clk), .clr(reset));
  Multiplexer #(.select(5), .width(32), .disabled(0), .enable("false")) multiplexer_1 (
    .in0(_0), .in1(_1), .in2(_2), .in3(_3), .in4(_4), .in5(_5), .in6(_6), .in7(_7), .in8(_8), .in9(_9),
    .in10(_10), .in11(_11), .in12(_12), .in13(_13), .in14(_14), .in15(_15), .in16(_16), .in17(_17),
    .in18(_18), .in19(_19), .in20(_20), .in21(_21), .in22(_22), .in23(_23), .in24(_24), .in25(_25),
    .in26(_26), .in27(_27), .in28(_28), .in29(_29), .in30(_30), .in31(_31), .out(RD1), .sel(in_4));
  Multiplexer #(.select(5), .width(32), .disabled(0), .enable("false")) multiplexer_2 (
    .in0(_0), .in1(_1), .in2(_2), .in3(_3), .in4(_4), .in5(_5), .in6(_6), .in7(_7), .in8(_8), .in9(_9),
    .in10(_10), .in11(_11), .in12(_12), .in13(_13), .in14(_14), .in15(_15), .in16(_16), .in17(_17),
    .in18(_18), .in19(_19), .in20(_20), .in21(_21), .in22(_22), .in23(_23), .in24(_24), .in25(_25),
    .in26(_26), .in27(_27), .in28(_28), .in29(_29), .in30(_30), .in31(_31), .out(RD2), .sel(in_5));

  // Other names for the same wires on the sheet: a1[4:0] = in_4; a2[4:0] = in_5
endmodule
