// Logisim project P0_L1_ftoi.circ as structural Verilog: 1 circuit, main circuit ftoi
module ftoi (
  input  [15:0] in_1,
  output [31:0] out_2
);

  wire and_1_out, and_2_out, comparator_1_lt, comparator_2_eq, comparator_3_eq, comparator_4_lt, not_1_out,
       not_2_out, or_1_out;
  wire [4:0] E, subtractor_2_out, subtractor_3_out;
  wire [31:0] adder_1_out, bit_extender_1_out, bit_extender_2_out, multiplexer_1_out, multiplexer_2_out,
       not_3_out, shifter_1_out, shifter_2_out;

  Subtractor #(.width(5)) subtractor_1 (.a(in_1[14:10]), .b(5'b01111), .out(E));  // open: bin, bout
  Comparator #(.width(5), .mode("unsigned")) comparator_1 (.a(E), .b(5'b01010), .lt(comparator_1_lt));  // open: gt, eq
  assign bit_extender_1_out = {{21{1'b0}}, {1'b1, in_1[9:0]}};  // Bit_Extender bit_extender_1
  Subtractor #(.width(5)) subtractor_2 (.a(E), .b(5'b01010), .out(subtractor_2_out));  // open: bin, bout
  assign bit_extender_2_out = {{21{1'b0}}, {1'b1, in_1[9:0]}};  // Bit_Extender bit_extender_2
  Subtractor #(.width(5)) subtractor_3 (.a(5'b01010), .b(E), .out(subtractor_3_out));  // open: bin, bout
  Shifter #(.width(32)) shifter_1 (.in(bit_extender_1_out), .\dist (subtractor_2_out), .out(shifter_1_out));
  Shifter #(.width(32), .shift("lr")) shifter_2 (
    .in(bit_extender_2_out), .\dist (subtractor_3_out), .out(shifter_2_out));
  Multiplexer #(.width(32), .enable("false")) multiplexer_1 (
    .in0(shifter_1_out), .in1(shifter_2_out), .out(multiplexer_1_out), .sel(comparator_1_lt));
  Comparator #(.width(5), .mode("unsigned")) comparator_2 (
    .a({5{1'b1}}), .b(in_1[14:10]), .eq(comparator_2_eq));  // open: gt, lt
  Comparator #(.width(5), .mode("unsigned")) comparator_3 (
    .a({5{1'b0}}), .b(in_1[14:10]), .eq(comparator_3_eq));  // open: gt, lt
  not not_1 (not_1_out, comparator_2_eq);
  not not_2 (not_2_out, comparator_3_eq);
  and and_1 (and_1_out, not_1_out, not_2_out);
  Comparator #(.width(5), .mode("unsigned")) comparator_4 (
    .a(in_1[14:10]), .b(5'b01111), .lt(comparator_4_lt));  // open: gt, eq
  assign not_3_out = ~multiplexer_1_out;  // NOT_Gate not_3, 32 bits wide
  and and_2 (and_2_out, and_1_out, comparator_4_lt);
  Adder #(.width(32)) adder_1 (.a(not_3_out), .b(32'h1), .out(adder_1_out));  // open: cin, cout
  Multiplexer #(.width(32), .enable("false")) multiplexer_2 (
    .in0(multiplexer_1_out), .in1(adder_1_out), .out(multiplexer_2_out), .sel(in_1[15]));
  or or_1 (or_1_out, comparator_2_eq, comparator_3_eq, and_2_out);
  Multiplexer #(.width(32), .enable("false")) multiplexer_3 (
    .in0(multiplexer_2_out), .in1({32{1'b0}}), .out(out_2), .sel(or_1_out));

  // Other names for the same wires on the sheet: _11[9:0] = in_1[9:0]; fra[9:0] = in_1[9:0]; exp[4:0] = in_1[14:10];
  //   sign = in_1[15]

  // Notes on the sheet:
  //   最终幂次大于等于10
  //   最终幂次小于10
endmodule
