// Logisim project P0_L1_navigation_2020.circ as structural Verilog: 2 circuits, main circuit navigation
// reset
module navigation (
  input  [1:0] direct,
  input  clk,
  input  reset,
  output arrive,
  output hit
);

  wire comparator_1_eq, comparator_3_eq;
  wire [2:0] pre_q, state_q, \状态转化_1_transfer ;
  wire [7:0] counter_1_q;

  \状态转化  \u_状态转化_1  (.state(state_q), .di(direct), .transfer(\状态转化_1_transfer ));
  Counter counter_1 (.Q(counter_1_q), .clk(clk), .clr(reset));  // open: load, D, count, carry
  Register #(.width(3)) state (.D(\状态转化_1_transfer ), .Q(state_q), .clk(clk), .clr(reset));  // open: en
  Register #(.width(3)) pre (.D(state_q), .Q(pre_q), .clk(clk), .clr(reset));  // open: en
  Comparator #(.width(3), .mode("unsigned")) comparator_1 (
    .a(state_q), .b(pre_q), .eq(comparator_1_eq));  // open: gt, lt
  Comparator #(.width(3), .mode("unsigned")) comparator_2 (.a(state_q), .b(3'b100), .eq(arrive));  // open: gt, lt
  Multiplexer multiplexer_1 (.in0(comparator_1_eq), .in1(1'b0), .out(hit), .sel(comparator_3_eq));  // open: en
  Comparator #(.mode("unsigned")) comparator_3 (.a(counter_1_q), .b({8{1'b0}}), .eq(comparator_3_eq));  // open: gt, lt

  // Notes on the sheet:
  //   要考虑到状态同步更新的问题，可以设置一个pre用来存储上一个状态
endmodule

module \状态转化  (
  input  [2:0] state,
  input  [1:0] di,
  output [2:0] transfer
);

  wire and_1_out, and_2_out, and_3_out, and_4_out, and_5_out, and_6_out, and_7_out, and_8_out, and_9_out,
       and_10_out, and_11_out, and_12_out, and_13_out, and_14_out, and_15_out, and_16_out, and_17_out,
       and_18_out, and_19_out, and_20_out, and_21_out, and_22_out, and_23_out, and_24_out, and_25_out,
       and_26_out, and_27_out, and_28_out, and_29_out, and_30_out, and_31_out, and_32_out, not_1_out,
       not_2_out, not_3_out, not_4_out, not_5_out, not_6_out, not_7_out, not_8_out, not_9_out, not_10_out,
       not_11_out, not_12_out, not_13_out, not_14_out, not_15_out, not_16_out, not_17_out, not_18_out,
       or_1_out, or_2_out, or_3_out, or_4_out, or_5_out, or_7_out, or_8_out, or_9_out, or_11_out, or_12_out;

  not not_1 (not_1_out, state[0]);
  not not_2 (not_2_out, di[1]);
  not not_3 (not_3_out, di[1]);
  not not_4 (not_4_out, di[0]);
  not not_5 (not_5_out, state[1]);
  not not_6 (not_6_out, di[1]);
  not not_7 (not_7_out, state[0]);
  not not_8 (not_8_out, di[1]);
  not not_9 (not_9_out, di[0]);
  not not_10 (not_10_out, state[0]);
  not not_11 (not_11_out, di[0]);
  not not_12 (not_12_out, state[2]);
  not not_13 (not_13_out, state[1]);
  and and_1 (and_1_out, state[1], not_1_out);
  and and_2 (and_2_out, and_1_out, and_3_out);
  and and_3 (and_3_out, not_2_out, di[0]);
  and and_4 (and_4_out, state[1], state[0]);
  and and_5 (and_5_out, and_4_out, and_6_out);
  and and_6 (and_6_out, not_3_out, not_4_out);
  and and_7 (and_7_out, state[2], state[0]);
  and and_8 (and_8_out, state[2], state[1]);
  and and_9 (and_9_out, not_5_out, state[0]);
  and and_10 (and_10_out, and_9_out, not_14_out);
  not not_14 (not_14_out, di[1]);
  and and_11 (and_11_out, state[0], not_6_out);
  and and_12 (and_12_out, and_11_out, di[0]);
  and and_13 (and_13_out, state[1], not_7_out);
  and and_14 (and_14_out, and_13_out, and_15_out);
  and and_15 (and_15_out, not_8_out, not_9_out);
  and and_16 (and_16_out, state[1], not_10_out);
  and and_17 (and_17_out, and_16_out, and_18_out);
  and and_18 (and_18_out, di[1], di[0]);
  and and_19 (and_19_out, state[1], state[0]);
  and and_20 (and_20_out, and_19_out, and_21_out);
  and and_21 (and_21_out, di[1], not_11_out);
  and and_22 (and_22_out, state[2], state[0]);
  and and_23 (and_23_out, not_12_out, not_13_out);
  and and_24 (and_24_out, and_23_out, not_15_out);
  not not_15 (not_15_out, state[0]);
  not not_16 (not_16_out, di[1]);
  and and_25 (and_25_out, not_16_out, not_17_out);
  not not_17 (not_17_out, di[0]);
  or or_1 (or_1_out, and_2_out, and_5_out);
  or or_2 (or_2_out, and_7_out, and_8_out);
  or or_3 (or_3_out, and_10_out, and_12_out);
  or or_4 (or_4_out, and_14_out, and_17_out);
  or or_5 (or_5_out, and_20_out, and_22_out);
  and and_26 (and_26_out, state[2], state[1]);
  and and_27 (and_27_out, and_24_out, and_25_out);
  and and_28 (and_28_out, state[0], di[0]);
  and and_29 (and_29_out, state[1], di[1]);
  not not_18 (not_18_out, di[0]);
  or or_6 (transfer[2], or_1_out, or_2_out);
  or or_7 (or_7_out, or_3_out, or_4_out);
  or or_8 (or_8_out, or_5_out, and_26_out);
  or or_9 (or_9_out, and_27_out, and_28_out);
  and and_30 (and_30_out, and_29_out, not_18_out);
  and and_31 (and_31_out, state[2], state[0]);
  and and_32 (and_32_out, state[2], state[1]);
  or or_10 (transfer[1], or_7_out, or_8_out);
  or or_11 (or_11_out, or_9_out, and_30_out);
  or or_12 (or_12_out, and_31_out, and_32_out);
  or or_13 (transfer[0], or_11_out, or_12_out);
endmodule
