// Logisim project plusCPU.circ as structural Verilog: 11 circuits, main circuit main
module GRF (
  input  reset,
  input  WE,
  input  clk,
  input  [4:0] in_4,
  input  [4:0] in_5,
  input  [4:0] A3,
  input  [31:0] WD,
  output [31:0] RD1,
  output [31:0] RD2
);

  wire decoder_1_out0, decoder_1_out1, decoder_1_out2, decoder_1_out3, decoder_1_out4, decoder_1_out5,
       decoder_1_out6, decoder_1_out7, decoder_1_out8, decoder_1_out9, decoder_1_out10, decoder_1_out11,
       decoder_1_out12, decoder_1_out13, decoder_1_out14, decoder_1_out15, decoder_1_out16, decoder_1_out17,
       decoder_1_out18, decoder_1_out19, decoder_1_out20, decoder_1_out21, decoder_1_out22, decoder_1_out23,
       decoder_1_out24, decoder_1_out25, decoder_1_out26, decoder_1_out27, decoder_1_out28, decoder_1_out29,
       decoder_1_out30, decoder_1_out31;
  wire [31:0] _0, _1, _2, _3, _4, _5, _6, _7, _8, _9, _10, _11, _12, _13, _14, _15, _16, _17, _18, _19, _20,
       _21, _22, _23, _24, _25, _26, _27, _28, _29, _30, _31;

  Decoder #(.select(5), .disabled(0)) decoder_1 (
    .out0(decoder_1_out0), .out1(decoder_1_out1), .out2(decoder_1_out2), .out3(decoder_1_out3),
    .out4(decoder_1_out4), .out5(decoder_1_out5), .out6(decoder_1_out6), .out7(decoder_1_out7),
    .out8(decoder_1_out8), .out9(decoder_1_out9), .out10(decoder_1_out10), .out11(decoder_1_out11),
    .out12(decoder_1_out12), .out13(decoder_1_out13), .out14(decoder_1_out14), .out15(decoder_1_out15),
    .out16(decoder_1_out16), .out17(decoder_1_out17), .out18(decoder_1_out18), .out19(decoder_1_out19),
    .out20(decoder_1_out20), .out21(decoder_1_out21), .out22(decoder_1_out22), .out23(decoder_1_out23),
    .out24(decoder_1_out24), .out25(decoder_1_out25), .out26(decoder_1_out26), .out27(decoder_1_out27),
    .out28(decoder_1_out28), .out29(decoder_1_out29), .out30(decoder_1_out30), .out31(decoder_1_out31),
    .sel(A3), .en(WE));
  Register #(.width(32)) _0_zero (.D({32{1'b0}}), .en(decoder_1_out0), .Q(_0), .clk(clk), .clr(reset));
  Register #(.width(32)) _8_t0 (.D(WD), .en(decoder_1_out8), .Q(_8), .clk(clk), .clr(reset));
  Register #(.width(32)) _16_s0 (.D(WD), .en(decoder_1_out16), .Q(_16), .clk(clk), .clr(reset));
  Register #(.width(32)) _24_t8 (.D(WD), .en(decoder_1_out24), .Q(_24), .clk(clk), .clr(reset));
  Register #(.width(32)) _1_at (.D(WD), .en(decoder_1_out1), .Q(_1), .clk(clk), .clr(reset));
  Register #(.width(32)) _9_t1 (.D(WD), .en(decoder_1_out9), .Q(_9), .clk(clk), .clr(reset));
  Register #(.width(32)) _17_s1 (.D(WD), .en(decoder_1_out17), .Q(_17), .clk(clk), .clr(reset));
  Register #(.width(32)) _25_t9 (.D(WD), .en(decoder_1_out25), .Q(_25), .clk(clk), .clr(reset));
  Register #(.width(32)) _2_v0 (.D(WD), .en(decoder_1_out2), .Q(_2), .clk(clk), .clr(reset));
  Register #(.width(32)) _10_t2 (.D(WD), .en(decoder_1_out10), .Q(_10), .clk(clk), .clr(reset));
  Register #(.width(32)) _18_s2 (.D(WD), .en(decoder_1_out18), .Q(_18), .clk(clk), .clr(reset));
  Register #(.width(32)) _26_k0 (.D(WD), .en(decoder_1_out26), .Q(_26), .clk(clk), .clr(reset));
  Register #(.width(32)) _3_v1 (.D(WD), .en(decoder_1_out3), .Q(_3), .clk(clk), .clr(reset));
  Register #(.width(32)) _11_t3 (.D(WD), .en(decoder_1_out11), .Q(_11), .clk(clk), .clr(reset));
  Register #(.width(32)) _19_s3 (.D(WD), .en(decoder_1_out19), .Q(_19), .clk(clk), .clr(reset));
  Register #(.width(32)) _27_k1 (.D(WD), .en(decoder_1_out27), .Q(_27), .clk(clk), .clr(reset));
  Register #(.width(32)) _4_a0 (.D(WD), .en(decoder_1_out4), .Q(_4), .clk(clk), .clr(reset));
  Register #(.width(32)) _12_t4 (.D(WD), .en(decoder_1_out12), .Q(_12), .clk(clk), .clr(reset));
  Register #(.width(32)) _20_s4 (.D(WD), .en(decoder_1_out20), .Q(_20), .clk(clk), .clr(reset));
  Register #(.width(32)) _28_gp (.D(WD), .en(decoder_1_out28), .Q(_28), .clk(clk), .clr(reset));
  Register #(.width(32)) _5_a1 (.D(WD), .en(decoder_1_out5), .Q(_5), .clk(clk), .clr(reset));
  Register #(.width(32)) _13_t5 (.D(WD), .en(decoder_1_out13), .Q(_13), .clk(clk), .clr(reset));
  Register #(.width(32)) _21_s5 (.D(WD), .en(decoder_1_out21), .Q(_21), .clk(clk), .clr(reset));
  Register #(.width(32)) _29_sp (.D(WD), .en(decoder_1_out29), .Q(_29), .clk(clk), .clr(reset));
  Register #(.width(32)) _6_a2 (.D(WD), .en(decoder_1_out6), .Q(_6), .clk(clk), .clr(reset));
  Register #(.width(32)) _14_t6 (.D(WD), .en(decoder_1_out14), .Q(_14), .clk(clk), .clr(reset));
  Register #(.width(32)) _22_s6 (.D(WD), .en(decoder_1_out22), .Q(_22), .clk(clk), .clr(reset));
  Register #(.width(32)) _30_fp (.D(WD), .en(decoder_1_out30), .Q(_30), .clk(clk), .clr(reset));
  Register #(.width(32)) _7_a3 (.D(WD), .en(decoder_1_out7), .Q(_7), .clk(clk), .clr(reset));
  Register #(.width(32)) _15_t7 (.D(WD), .en(decoder_1_out15), .Q(_15), .clk(clk), .clr(reset));
  Register #(.width(32)) _23_s7 (.D(WD), .en(decoder_1_out23), .Q(_23), .clk(clk), .clr(reset));
  Register #(.width(32)) _31_ra (.D(WD), .en(decoder_1_out31), .Q(_31), .clk(clk), .clr(reset));
  Multiplexer #(.select(5), .width(32), .disabled(0), .enable("false")) multiplexer_1 (
    .in0(_0), .in1(_1), .in2(_2), .in3(_3), .in4(_4), .in5(_5), .in6(_6), .in7(_7), .in8(_8), .in9(_9),
    .in10(_10), .in11(_11), .in12(_12), .in13(_13), .in14(_14), .in15(_15), .in16(_16), .in17(_17),
    .in18(_18), .in19(_19), .in20(_20), .in21(_21), .in22(_22), .in23(_23), .in24(_24), .in25(_25),
    .in26(_26), .in27(_27), .in28(_28), .in29(_29), .in30(_30), .in31(_31), .out(RD1), .sel(in_4));
  Multiplexer #(.select(5), .width(32), .disabled(0), .enable("false")) multiplexer_2 (
    .in0(_0), .in1(_1), .in2(_2), .in3(_3), .in4(_4), .in5(_5), .in6(_6), .in7(_7), .in8(_8), .in9(_9),
    .in10(_10), .in11(_11), .in12(_12), .in13(_13), .in14(_14), .in15(_15), .in16(_16), .in17(_17),
    .in18(_18), .in19(_19), .in20(_20), .in21(_21), .in22(_22), .in23(_23), .in24(_24), .in25(_25),
    .in26(_26), .in27(_27), .in28(_28), .in29(_29), .in30(_30), .in31(_31), .out(RD2), .sel(in_5));

  // Other names for the same wires on the sheet: a1[4:0] = in_4; a2[4:0] = in_5
endmodule

module main (
  input  Reset,
  output [31:0] out_2,
  output out_3,
  output [4:0] out_4,
  output [31:0] out_5,
  output out_6,
  output [4:0] out_7,
  output [31:0] out_8
);

  wire ALU, ALU_t, ALU_t_t, and_2_out, BSel, clk, EXTOp, isBeq, isSlt, PCSrc;
  wire [2:0] A3Sel, Br, DM_bit_type, WDSel;
  wire [3:0] ALU_C;
  wire [4:0] cut_1_rd, cut_1_rs, cut_1_rt, shamt;
  wire [15:0] _15_0imm;
  wire [25:0] _25_0;
  wire [31:0] ALUout, DM_origin, DMout, EXTout, in_dm_1_in_dm, judge_slt, multiplexer_3_out, npc_1_pc_prime,
       PC_4, PC_q, RD1;

  Clock clock_1 (.out(clk));
  Register #(.width(32)) PC (.D(npc_1_pc_prime), .Q(PC_q), .clk(clk), .clr(Reset));  // open: en
  NPC npc_1 (
    .PC_prime(npc_1_pc_prime), .PC(PC_q), .PC_4(PC_4), .Br(Br), ._15_0imm(_15_0imm), .PCSrc(PCSrc),
    .imm25_0(_25_0), .RA(RD1));
  and and_1 (PCSrc, ALU_t, isBeq);
  IM im_1 (.PC(PC_q), .R_I(out_2));
  CU cu_1 (
    .Instr(out_2), .Br(Br), .A3Sel(A3Sel), .WDSel(WDSel), .RFWr(out_3), .EXTop(EXTOp), .BSel(BSel),
    .DMWr(out_6), .ALUControl(ALU_C), .beq(isBeq), .out_11(DM_bit_type), .slt(isSlt));
  cut cut_1 (.Instr(out_2), .shamt(shamt), .rt(cut_1_rt), .rd(cut_1_rd), .rs(cut_1_rs), .imm(_15_0imm), .target(_25_0));
  EXT ext_1 (.imm(_15_0imm), .out_3(EXTout), .EXTOp(EXTOp));
  Multiplexer #(.select(3), .width(5), .enable("false")) multiplexer_1 (
    .in0(cut_1_rt), .in1(cut_1_rd), .in2({5{1'b1}}), .out(out_4), .sel(A3Sel));  // open: in3, in4, in5, in6, in7
  Multiplexer #(.select(3), .width(32), .enable("false")) multiplexer_2 (
    .in0({ALUout[31:7], out_7, ALUout[1:0]}), .in1(DMout), .in2(PC_4), .in3(judge_slt), .out(out_5),
    .sel(WDSel));  // open: in4, in5, in6, in7
  GRF grf_1 (
    .reset(Reset), .A3(out_4), .WD(out_5), .RD1(RD1), .WE(out_3), .in_4(cut_1_rs), .in_5(cut_1_rt),
    .clk(clk), .RD2(out_8));
  Multiplexer #(.width(32), .enable("false")) multiplexer_3 (
    .in0(out_8), .in1(EXTout), .out(multiplexer_3_out), .sel(BSel));
  Multiplexer #(.width(32), .enable("false")) multiplexer_4 (
    .in0({32{1'b0}}), .in1(32'h1), .out(judge_slt), .sel(and_2_out));
  and and_2 (and_2_out, ALU, isSlt);
  ALU alu_1 (
    .ScrA(RD1), .ScrB(multiplexer_3_out), .out_8({ALUout[31:7], out_7, ALUout[1:0]}), .ALUControl(ALU_C),
    .out_6(ALU_t), .in_2(shamt), .a_b(ALU_t_t), .a_b_2(ALU));
  IN_DM in_dm_1 (
    .NewData(out_8), .OldValue_DMtmp(DM_origin), .in_DM(in_dm_1_in_dm),
    .addr({ALUout[31:7], out_7, ALUout[1:0]}), .bit_type(DM_bit_type));
  DM dm_1 (.A(out_7), .WD(in_dm_1_in_dm), .WE(out_6), .RD(DM_origin), .clk(clk), .reset(Reset));
  OUT_DM out_dm_1 (.data(DM_origin), .out_DM(DMout), .addr({ALUout[31:7], out_7, ALUout[1:0]}), .bit_type(DM_bit_type));

  // Other names for the same wires on the sheet: ALUout[6:2] = out_7; MemAddr[4:0] = out_7; Instr[31:0] = out_2;
  //   MemWrite = out_6; RD2[31:0] = out_8; RegAddr[4:0] = out_4; RegData[31:0] = out_5; RegWrite = out_3

  // Notes on the sheet:
  //   rs
  //   25:21
  //   rt
  //   20:16
  //   rd
  //   15:11
  //   jal
endmodule

module IM (
  input  [31:0] PC,
  output [31:0] R_I
);

  ROM #(.addrWidth(24), .dataWidth(32)) rom_1 (.addr(PC[25:2]), .data(R_I));  // open: sel

  // Notes on the sheet:
  //   contents of rom_1 (hex, n*v repeats v):
  //   34080000 3411ffff 34120002 34130003 34140004 34150005 ad110000 a5120000 a5130002 ad110000 a1120000
  //   a1130001 a1140002 a1150003 811a0000 811b0001 811c0002 811d0003 851e0000 851f0002 8d010000
endmodule

module DM (
  input  WE,
  input  [4:0] A,
  input  clk,
  input  [31:0] WD,
  input  reset,
  output [31:0] RD
);

  RAM #(.addrWidth(5), .dataWidth(32), .bus("separate")) ram_1 (
    .addr(A), .din(WD), .data(RD), .str(WE), .clk(clk), .clr(reset));  // open: sel, ld
endmodule

module CU (
  input  [31:0] Instr,
  output [2:0] Br,
  output [2:0] A3Sel,
  output [2:0] WDSel,
  output RFWr,
  output EXTop,
  output BSel,
  output DMWr,
  output [3:0] ALUControl,
  output beq,
  output [2:0] out_11,
  output slt
);

  wire addi, addu, \and , BRANCH, comparator_2_eq, comparator_3_eq, comparator_4_eq, comparator_5_eq,
       comparator_6_eq, comparator_7_eq, comparator_8_eq, j, jal, jalr, jr, lb, lh, LOAD, lui, lw, or_1_out,
       or_2_out, or_3_out, or_4_out, or_5_out, or_6_out, ori, R, sb, sh, sll, subu, sw;

  buf or_1 (or_1_out, ori);  // OR_Gate
  Comparator #(.width(6), .mode("unsigned")) comparator_1 (.a(Instr[31:26]), .b({6{1'b0}}), .eq(R));  // open: gt, lt
  Comparator #(.width(6)) comparator_2 (.a(Instr[5:0]), .b(6'b100001), .eq(comparator_2_eq));  // open: gt, lt
  Comparator #(.width(6)) comparator_3 (.a(Instr[5:0]), .b(6'b100011), .eq(comparator_3_eq));  // open: gt, lt
  Comparator #(.width(6)) comparator_4 (.a(Instr[5:0]), .b({6{1'b0}}), .eq(comparator_4_eq));  // open: gt, lt
  Comparator #(.width(6)) comparator_5 (.a(Instr[5:0]), .b(6'b001000), .eq(comparator_5_eq));  // open: gt, lt
  Comparator #(.width(6)) comparator_6 (.a(Instr[5:0]), .b(6'b100100), .eq(comparator_6_eq));  // open: gt, lt
  Comparator #(.width(6)) comparator_7 (.a(Instr[5:0]), .b(6'b101010), .eq(comparator_7_eq));  // open: gt, lt
  Comparator #(.width(6)) comparator_8 (.a(Instr[5:0]), .b(6'b001001), .eq(comparator_8_eq));  // open: gt, lt
  buf or_2 (or_2_out, subu);  // OR_Gate
  buf or_3 (or_3_out, \and );  // OR_Gate
  or or_4 (or_4_out, lh, sh);
  or or_5 (or_5_out, sb, lb);
  and and_1 (addu, comparator_2_eq, R);
  and and_2 (subu, comparator_3_eq, R);
  and and_3 (sll, comparator_4_eq, R);
  and and_4 (jr, comparator_5_eq, R);
  and and_5 (\and , comparator_6_eq, R);
  and and_6 (slt, comparator_7_eq, R);
  and and_7 (jalr, comparator_8_eq, R);
  Pull_Resistor pull_resistor_1 (.node(ALUControl));
  Priority_Encoder #(.select(4)) priority_encoder_1 (
    .in1(or_2_out), .in2(or_3_out), .in3(or_1_out), .in4(lui), .in5(sll), .out(ALUControl));  // open: in0, in6, in7, in8, in9, in10, in11, in12, in13, in14, in15, gs, en_out, en_in
  Priority_Encoder priority_encoder_2 (
    .in1(R), .in2(jal), .out(A3Sel));  // open: in0, in3, in4, in5, in6, in7, en_in, gs, en_out
  Pull_Resistor pull_resistor_2 (.node(A3Sel));
  nor nor_1 (RFWr, DMWr, BRANCH, jr, j);
  nor nor_2 (BSel, R, BRANCH, j, jal);
  Pull_Resistor pull_resistor_3 (.node(out_11));
  Priority_Encoder priority_encoder_3 (
    .in1(or_4_out), .in2(or_5_out), .out(out_11));  // open: in0, in3, in4, in5, in6, in7, en_in, gs, en_out
  Comparator #(.width(6), .mode("unsigned")) comparator_9 (.a(Instr[31:26]), .b(6'b001101), .eq(ori));  // open: gt, lt
  Comparator #(.width(6), .mode("unsigned")) comparator_10 (.a(Instr[31:26]), .b(6'b001111), .eq(lui));  // open: gt, lt
  Comparator #(.width(6), .mode("unsigned")) comparator_11 (
    .a(Instr[31:26]), .b(6'b001000), .eq(addi));  // open: gt, lt
  or or_6 (or_6_out, jal, jalr);
  buf or_7 (BRANCH, beq);  // OR_Gate
  Comparator #(.width(6), .mode("unsigned")) comparator_12 (.a(Instr[31:26]), .b(6'b000100), .eq(beq));  // open: gt, lt
  Priority_Encoder priority_encoder_4 (
    .in1(beq), .in2(j), .in3(jal), .in4(jr), .in5(jalr), .out(Br));  // open: in0, in6, in7, en_in, gs, en_out
  Priority_Encoder priority_encoder_5 (
    .in1(LOAD), .in2(or_6_out), .in3(slt), .out(WDSel));  // open: in0, in4, in5, in6, in7, en_in, gs, en_out
  or or_8 (EXTop, DMWr, LOAD, addi);
  Pull_Resistor pull_resistor_4 (.node(Br));
  Pull_Resistor pull_resistor_5 (.node(WDSel));
  or or_9 (DMWr, sw, sh, sb);
  Comparator #(.width(6), .mode("unsigned")) comparator_13 (.a(Instr[31:26]), .b(6'b101011), .eq(sw));  // open: gt, lt
  Comparator #(.width(6), .mode("unsigned")) comparator_14 (.a(Instr[31:26]), .b(6'b101001), .eq(sh));  // open: gt, lt
  Comparator #(.width(6), .mode("unsigned")) comparator_15 (.a(Instr[31:26]), .b(6'b101000), .eq(sb));  // open: gt, lt
  or or_10 (LOAD, lw, lh, lb);
  Comparator #(.width(6), .mode("unsigned")) comparator_16 (.a(Instr[31:26]), .b(6'b100011), .eq(lw));  // open: gt, lt
  Comparator #(.width(6), .mode("unsigned")) comparator_17 (.a(Instr[31:26]), .b(6'b100001), .eq(lh));  // open: gt, lt
  Comparator #(.width(6), .mode("unsigned")) comparator_18 (.a(Instr[31:26]), .b(6'b100000), .eq(lb));  // open: gt, lt
  Comparator #(.width(6), .mode("unsigned")) comparator_19 (.a(Instr[31:26]), .b(6'b000010), .eq(j));  // open: gt, lt
  Comparator #(.width(6), .mode("unsigned")) comparator_20 (.a(Instr[31:26]), .b(6'b000011), .eq(jal));  // open: gt, lt

  // Other names for the same wires on the sheet: DMtype[2:0] = out_11; func[5:0] = Instr[5:0];
  //   opcode[5:0] = Instr[31:26]; STORE = DMWr

  // Notes on the sheet:
  //   jalr属于R
  //   add / sub / and / or/ 
  //   20:16 / 15:11/ 固定写入$ra)  
  //   add里面已经包含存取指令地址加减
  //   写入GRF
  //   不写入reg的，非写使能
  //   不用立即数作为ALU_b的
  //   DM_bit
  //   写入存储器
  //   pc+4/b_/j_
  //   ALUout / DMout /PC4
  //   符号拓展的
  //   选择PC值
  //   GRF写入的数据类型选择
endmodule

module cut (
  input  [31:0] Instr,
  output [4:0] shamt,
  output [4:0] rs,
  output [4:0] rt,
  output [4:0] rd,
  output [15:0] imm,
  output [25:0] target
);


  assign imm = Instr[15:0];
  assign rd = Instr[15:11];
  assign rs = Instr[25:21];
  assign rt = Instr[20:16];
  assign shamt = Instr[10:6];
  assign target = Instr[25:0];

  // Notes on the sheet:
  //   R型
  //   I型
endmodule

module EXT (
  input  [15:0] imm,
  input  EXTOp,
  output [31:0] out_3
);

  wire [31:0] bit_extender_1_out, bit_extender_2_out;

  assign bit_extender_1_out = {{16{1'b0}}, imm};  // Bit_Extender bit_extender_1
  assign bit_extender_2_out = {{16{imm[15]}}, imm};  // Bit_Extender bit_extender_2
  Multiplexer #(.width(32), .enable("false")) multiplexer_1 (
    .in0(bit_extender_1_out), .in1(bit_extender_2_out), .out(out_3), .sel(EXTOp));
endmodule

module ALU (
  input  [3:0] ALUControl,
  input  [4:0] in_2,
  input  [31:0] ScrA,
  input  [31:0] ScrB,
  output a_b,
  output out_6,
  output a_b_2,
  output [31:0] out_8
);

  wire [31:0] adder_1_out, and_1_out, or_1_out, shifter_1_out, shifter_2_out, subtractor_1_out;

  Adder #(.width(32)) adder_1 (.a(ScrA), .b(ScrB), .out(adder_1_out));  // open: cin, cout
  Subtractor #(.width(32)) subtractor_1 (.a(ScrA), .b(ScrB), .out(subtractor_1_out));  // open: bin, bout
  assign and_1_out = ScrA & ScrB;  // AND_Gate and_1, 32 bits wide
  assign or_1_out = ScrA | ScrB;  // OR_Gate or_1, 32 bits wide
  Shifter #(.width(32)) shifter_1 (.in(ScrB), .\dist (5'b10000), .out(shifter_1_out));
  Shifter #(.width(32)) shifter_2 (.in(ScrB), .\dist (in_2), .out(shifter_2_out));
  Comparator #(.width(32)) comparator_1 (.a(subtractor_1_out), .b({32{1'b0}}), .gt(a_b), .eq(out_6), .lt(a_b_2));
  Multiplexer #(.select(4), .width(32), .enable("false")) multiplexer_1 (
    .in0(adder_1_out), .in1(subtractor_1_out), .in2(and_1_out), .in3(or_1_out), .in4(shifter_1_out),
    .in5(shifter_2_out), .out(out_8), .sel(ALUControl));  // open: in6, in7, in8, in9, in10, in11, in12, in13, in14, in15

  // Other names for the same wires on the sheet: shamt[4:0] = in_2

  // Notes on the sheet:
  //   lui,加载到高位
endmodule

module NPC (
  input  [31:0] PC,
  input  [25:0] imm25_0,
  input  [31:0] RA,
  input  [15:0] _15_0imm,
  input  PCSrc,
  input  [2:0] Br,
  output [31:0] PC_prime,
  output [31:0] PC_4
);

  wire SLT;
  wire [31:0] adder_2_out, bit_extender_1_out, multiplexer_1_out, multiplexer_2_out, shifter_1_out,
       subtractor_1_out;

  assign bit_extender_1_out = {{16{_15_0imm[15]}}, _15_0imm};  // Bit_Extender bit_extender_1
  Shifter #(.width(32)) shifter_1 (.in(bit_extender_1_out), .\dist (5'b00010), .out(shifter_1_out));
  Adder #(.width(32)) adder_1 (.a(PC), .b(32'h4), .out(PC_4));  // open: cin, cout
  Adder #(.width(32)) adder_2 (.a(PC_4), .b(shifter_1_out), .out(adder_2_out));  // open: cin, cout
  Multiplexer #(.width(32), .enable("false")) multiplexer_1 (
    .in0(PC_4), .in1(adder_2_out), .out(multiplexer_1_out), .sel(PCSrc));
  Multiplexer #(.select(3), .width(32), .enable("false")) multiplexer_2 (
    .in0(PC_4), .in1(multiplexer_1_out), .in2({PC[31:28], imm25_0, 2'b00}),
    .in3({PC[31:28], imm25_0, 2'b00}), .in4(RA), .in5(RA), .out(multiplexer_2_out), .sel(Br));  // open: in6, in7
  Comparator #(.width(32)) comparator_1 (.a(multiplexer_2_out), .b(32'h3000), .gt(SLT));  // open: eq, lt
  Subtractor #(.width(32)) subtractor_1 (
    .a(multiplexer_2_out), .b(32'h3000), .out(subtractor_1_out));  // open: bin, bout
  Multiplexer #(.width(32), .enable("false")) multiplexer_3 (
    .in0(multiplexer_2_out), .in1(subtractor_1_out), .out(PC_prime), .sel(SLT));

  // Other names for the same wires on the sheet: JAL_J[31:2] = {PC[31:28], imm25_0}

  // Notes on the sheet:
  //   _B
  //   测试这两个值的时候，加3000
  //   branch是不用加的。标签值是相对值，j这个是绝值
  //   JAL/J
endmodule

module IN_DM (
  input  [2:0] bit_type,
  input  [31:0] addr,
  input  [31:0] NewData,
  input  [31:0] OldValue_DMtmp,
  output [31:0] in_DM
);

  wire [15:0] multiplexer_2_out;
  wire [31:0] _SB, _SH, and_1_out, and_2_out, and_3_out, and_4_out, bit_extender_1_out, bit_extender_2_out,
       bit_extender_3_out, multiplexer_3_out, multiplexer_4_out, or_1_out, or_2_out, shifter_1_out,
       shifter_2_out, shifter_3_out, shifter_4_out, shifter_5_out;

  Multiplexer #(.select(3), .width(32), .enable("false")) multiplexer_1 (
    .in0(NewData), .in1(_SH), .in2(_SB), .out(in_DM), .sel(bit_type));  // open: in3, in4, in5, in6, in7
  Multiplexer #(.width(16), .enable("false")) multiplexer_2 (
    .in0(OldValue_DMtmp[31:16]), .in1(OldValue_DMtmp[15:0]), .out(multiplexer_2_out), .sel(addr[1]));
  assign bit_extender_1_out = {{16{1'b0}}, NewData[15:0]};  // Bit_Extender bit_extender_1
  assign and_1_out = OldValue_DMtmp & 32'hffffff00;  // AND_Gate and_1, 32 bits wide
  assign and_2_out = OldValue_DMtmp & 32'hffff00ff;  // AND_Gate and_2, 32 bits wide
  assign and_3_out = OldValue_DMtmp & 32'hff00ffff;  // AND_Gate and_3, 32 bits wide
  assign and_4_out = OldValue_DMtmp & 32'hffffff;  // AND_Gate and_4, 32 bits wide
  assign bit_extender_2_out = {{24{1'b0}}, NewData[7:0]};  // Bit_Extender bit_extender_2
  assign bit_extender_3_out = {{16{1'b0}}, multiplexer_2_out};  // Bit_Extender bit_extender_3
  Shifter #(.width(32)) shifter_1 (.in(bit_extender_2_out), .\dist (5'b01000), .out(shifter_1_out));
  Shifter #(.width(32)) shifter_2 (.in(bit_extender_2_out), .\dist (5'b10000), .out(shifter_2_out));
  Shifter #(.width(32)) shifter_3 (.in(bit_extender_2_out), .\dist (5'b11000), .out(shifter_3_out));
  Shifter #(.width(32)) shifter_4 (.in(bit_extender_3_out), .\dist (5'b10000), .out(shifter_4_out));
  Shifter #(.width(32)) shifter_5 (.in(bit_extender_1_out), .\dist (5'b10000), .out(shifter_5_out));
  assign or_1_out = shifter_4_out | bit_extender_1_out;  // OR_Gate or_1, 32 bits wide
  assign or_2_out = bit_extender_3_out | shifter_5_out;  // OR_Gate or_2, 32 bits wide
  Multiplexer #(.select(2), .width(32), .enable("false")) multiplexer_3 (
    .in0(and_1_out), .in1(and_2_out), .in2(and_3_out), .in3(and_4_out), .out(multiplexer_3_out),
    .sel(addr[1:0]));
  Multiplexer #(.select(2), .width(32), .enable("false")) multiplexer_4 (
    .in0(bit_extender_2_out), .in1(shifter_1_out), .in2(shifter_2_out), .in3(shifter_3_out),
    .out(multiplexer_4_out), .sel(addr[1:0]));
  Multiplexer #(.width(32), .enable("false")) multiplexer_5 (.in0(or_1_out), .in1(or_2_out), .out(_SH), .sel(addr[1]));
  assign _SB = multiplexer_3_out | multiplexer_4_out;  // OR_Gate or_3, 32 bits wide

  // Other names for the same wires on the sheet: _SW[31:0] = NewData; byte[1:0] = addr[1:0];
  //   OldData[31:0] = OldValue_DMtmp
endmodule

module OUT_DM (
  input  [31:0] addr,
  input  [2:0] bit_type,
  input  [31:0] data,
  output [31:0] out_DM
);

  wire [7:0] multiplexer_2_out;
  wire [15:0] multiplexer_1_out;
  wire [31:0] _LB, _LH;

  Multiplexer #(.width(16), .enable("false")) multiplexer_1 (
    .in0(data[15:0]), .in1(data[31:16]), .out(multiplexer_1_out), .sel(addr[1]));
  Multiplexer #(.select(2), .width(8), .enable("false")) multiplexer_2 (
    .in0(data[7:0]), .in1(data[15:8]), .in2(data[23:16]), .in3(data[31:24]), .out(multiplexer_2_out),
    .sel(addr[1:0]));
  assign _LH = {{16{multiplexer_1_out[15]}}, multiplexer_1_out};  // Bit_Extender bit_extender_1
  assign _LB = {{24{multiplexer_2_out[7]}}, multiplexer_2_out};  // Bit_Extender bit_extender_2
  Multiplexer #(.select(3), .width(32), .enable("false")) multiplexer_3 (
    .in0(data), .in1(_LH), .in2(_LB), .out(out_DM), .sel(bit_type));  // open: in3, in4, in5, in6, in7

  // Other names for the same wires on the sheet: _LW[31:0] = data; out_bit_type[2:0] = bit_type
endmodule
