// Logisim project 1bit_swap.circ as structural Verilog: 2 circuits, main circuit main
module main (
  input  I1,
  input  I2,
  input  S,
  output _01,
  output _02
);

  wire and_1_out, and_2_out, and_3_out, and_4_out, not_1_out, not_2_out;

  not not_1 (not_1_out, S);
  not not_2 (not_2_out, S);
  and and_1 (and_1_out, I2, S);
  and and_2 (and_2_out, I1, not_1_out);
  and and_3 (and_3_out, I2, not_2_out);
  and and_4 (and_4_out, I1, S);
  swap swap_1 ();  // open: I1, I2, S, o1, o2
  or or_1 (_01, and_1_out, and_2_out);
  or or_2 (_02, and_3_out, and_4_out);
endmodule

module swap (
  input  I1,
  input  I2,
  input  S,
  output o1,
  output o2
);

  wire and_1_out, and_2_out, and_3_out, and_4_out, not_1_out, not_2_out;

  not not_1 (not_1_out, S);
  not not_2 (not_2_out, S);
  and and_1 (and_1_out, I2, S);
  and and_2 (and_2_out, I1, not_1_out);
  and and_3 (and_3_out, I2, not_2_out);
  and and_4 (and_4_out, I1, S);
  or or_1 (o1, and_1_out, and_2_out);
  or or_2 (o2, and_3_out, and_4_out);
endmodule
