// Logisim project 4bit_sort.circ as structural Verilog: 3 circuits, main circuit 4bit_sort
module _1bit_swap (
  input  I1,
  input  I2,
  input  S,
  output o1,
  output o2
);

  wire and_1_out, and_2_out, and_3_out, and_4_out, not_1_out, not_2_out;

  not not_1 (not_1_out, S);
  not not_2 (not_2_out, S);
  and and_1 (and_1_out, I2, S);
  and and_2 (and_2_out, I1, not_1_out);
  and and_3 (and_3_out, I2, not_2_out);
  and and_4 (and_4_out, I1, S);
  or or_1 (o1, and_1_out, and_2_out);
  or or_2 (o2, and_3_out, and_4_out);
endmodule

module _4bit_swap (
  input  [3:0] I1_B,
  input  [3:0] I2_B,
  input  in_3,
  output [3:0] out_4,
  output [3:0] out_5
);

  _1bit_swap u_1bit_swap_1 (.I1(I1_B[0]), .I2(I2_B[0]), .S(in_3), .o1(out_4[0]), .o2(out_5[0]));
  _1bit_swap u_1bit_swap_2 (.I1(I1_B[1]), .I2(I2_B[1]), .S(in_3), .o1(out_4[1]), .o2(out_5[1]));
  _1bit_swap u_1bit_swap_3 (.I1(I1_B[2]), .I2(I2_B[2]), .S(in_3), .o1(out_4[2]), .o2(out_5[2]));
  _1bit_swap u_1bit_swap_4 (.I1(I1_B[3]), .I2(I2_B[3]), .S(in_3), .o1(out_4[3]), .o2(out_5[3]));
endmodule

module _4bit_sort (
  input  [3:0] in_1,
  input  [3:0] in_2,
  input  [3:0] in_3,
  input  [3:0] in_4,
  output [3:0] out_5,
  output [3:0] out_6,
  output [3:0] out_7,
  output [3:0] out_8
);

  wire comparator_1_gt, comparator_2_gt, comparator_3_gt, comparator_4_gt, comparator_5_gt;
  wire [3:0] n4bit_swap_1_out_4, n4bit_swap_1_out_5, n4bit_swap_2_out_4, n4bit_swap_2_out_5,
       n4bit_swap_3_out_5, n4bit_swap_4_out_4;

  Comparator #(.width(4), .mode("unsigned")) comparator_1 (.a(in_1), .b(in_2), .gt(comparator_1_gt));  // open: eq, lt
  Comparator #(.width(4), .mode("unsigned")) comparator_2 (.a(in_3), .b(in_4), .gt(comparator_2_gt));  // open: eq, lt
  _4bit_swap u_4bit_swap_1 (
    .I1_B(in_1), .I2_B(in_2), .in_3(comparator_1_gt), .out_4(n4bit_swap_1_out_4), .out_5(n4bit_swap_1_out_5));
  _4bit_swap u_4bit_swap_2 (
    .I1_B(in_3), .I2_B(in_4), .in_3(comparator_2_gt), .out_4(n4bit_swap_2_out_4), .out_5(n4bit_swap_2_out_5));
  Comparator #(.width(4), .mode("unsigned")) comparator_3 (
    .a(n4bit_swap_1_out_4), .b(n4bit_swap_2_out_4), .gt(comparator_3_gt));  // open: eq, lt
  Comparator #(.width(4), .mode("unsigned")) comparator_4 (
    .a(n4bit_swap_1_out_5), .b(n4bit_swap_2_out_5), .gt(comparator_4_gt));  // open: eq, lt
  _4bit_swap u_4bit_swap_3 (
    .I1_B(n4bit_swap_1_out_4), .I2_B(n4bit_swap_2_out_4), .in_3(comparator_3_gt), .out_4(out_5),
    .out_5(n4bit_swap_3_out_5));
  _4bit_swap u_4bit_swap_4 (
    .I1_B(n4bit_swap_1_out_5), .I2_B(n4bit_swap_2_out_5), .in_3(comparator_4_gt), .out_4(n4bit_swap_4_out_4),
    .out_5(out_8));
  _4bit_swap u_4bit_swap_5 (
    .I1_B(n4bit_swap_3_out_5), .I2_B(n4bit_swap_4_out_4), .in_3(comparator_5_gt), .out_4(out_6), .out_5(out_7));
  Comparator #(.width(4), .mode("unsigned")) comparator_5 (
    .a(n4bit_swap_3_out_5), .b(n4bit_swap_4_out_4), .gt(comparator_5_gt));  // open: eq, lt
endmodule
