// Logisim project fblc_test.circ as structural Verilog: 1 circuit, main circuit main
module main (
  input  [2:0] in_1,
  output [3:0] out_2
);

  wire clk, comparator_2_lt, EN, SLT1, SLT2;
  wire [2:0] counter_1_q;
  wire [3:0] adder_1_out, multiplexer_1_out, now_q, pre_q;
  wire [5:0] counter_2_q, counter_3_q;

  Clock clock_1 (.out(clk));
  Adder #(.width(4)) adder_1 (.a(now_q), .b(pre_q), .out(adder_1_out));  // open: cin, cout
  Multiplexer #(.width(4)) multiplexer_1 (
    .in0(4'b0001), .in1(adder_1_out), .out(multiplexer_1_out), .sel(SLT1));  // open: en
  Register #(.width(4)) now (.D(multiplexer_1_out), .en(EN), .Q(now_q), .clk(clk));  // open: clr
  Counter #(.width(3), .max('h7), .ongoal("stay")) counter_1 (
    .Q(counter_1_q), .clk(clk));  // open: load, D, count, carry, clr
  Counter #(.width(6), .max('h3f), .ongoal("stay")) counter_2 (
    .Q(counter_2_q), .clk(clk));  // open: load, D, count, carry, clr
  Comparator #(.width(3), .mode("unsigned")) comparator_1 (.a(counter_1_q), .b(in_1), .eq(SLT2), .lt(EN));  // open: gt
  Comparator #(.width(6), .mode("unsigned")) comparator_2 (
    .a(counter_2_q), .b(6'b100000), .lt(comparator_2_lt));  // open: gt, eq
  Register #(.width(4)) pre (.D(now_q), .en(EN), .Q(pre_q), .clk(clk));  // open: clr
  Counter #(.width(6), .max('h3f), .ongoal("stay")) counter_3 (
    .Q(counter_3_q), .clk(clk));  // open: load, D, count, carry, clr
  Multiplexer #(.width(4)) multiplexer_2 (.in0(4'b0000), .in1(now_q), .out(out_2), .sel(SLT2));  // open: en
  Comparator #(.width(6), .mode("unsigned")) comparator_3 (.a(counter_3_q), .b(6'b000001), .gt(SLT1));  // open: eq, lt

  // Notes on the sheet:
  //   控制，超过时候时间阻塞
  //   slt2 未达到输出时一直为0
  //   32周期输出的条件
endmodule
