// Logisim project fibonacci.circ as structural Verilog: 2 circuits, main circuit main
module main (
  input  [2:0] in_1,
  output [3:0] out_2
);

  wire clock_1_out, comparator_1_lt, comparator_2_eq, comparator_2_lt, or_1_out;
  wire [2:0] counter_1_q;
  wire [3:0] adder_1_out, F_n_1_q, multiplexer_1_out;

  Clock clock_1 (.out(clock_1_out));
  Counter #(.width(3), .max('h7)) counter_1 (.Q(counter_1_q), .clk(or_1_out));  // open: load, D, count, carry, clr
  Comparator #(.width(3), .mode("unsigned")) comparator_1 (
    .a(3'b000), .b(counter_1_q), .lt(comparator_1_lt));  // open: gt, eq
  Comparator #(.width(3), .mode("unsigned")) comparator_2 (
    .a(in_1), .b(counter_1_q), .eq(comparator_2_eq), .lt(comparator_2_lt));  // open: gt
  Multiplexer #(.width(4)) multiplexer_1 (
    .in0(4'b0001), .in1(adder_1_out), .out(multiplexer_1_out), .sel(comparator_1_lt));  // open: en
  or or_1 (or_1_out, comparator_2_eq, comparator_2_lt, clock_1_out);
  Register #(.width(4)) F_n (.D(multiplexer_1_out), .Q(out_2), .clk(or_1_out));  // open: en, clr
  Register #(.width(4)) F_n_1 (.D(out_2), .Q(F_n_1_q), .clk(or_1_out));  // open: en, clr
  Adder #(.width(4)) adder_1 (.a(out_2), .b(F_n_1_q), .out(adder_1_out));  // open: cin, cout
endmodule

module test (
  output [3:0] out_1
);

  wire clock_1_out, counter_1_carry;
  wire [3:0] main_1_out_2;

  Counter #(.width(6), .max('h3f)) counter_1 (
    .carry(counter_1_carry), .clk(clock_1_out));  // open: load, D, count, Q, clr
  Clock clock_1 (.out(clock_1_out));
  main main_1 (.out_2(main_1_out_2));  // open: in_1
  Register #(.width(4)) register_1 (.D(main_1_out_2), .Q(out_1), .clk(counter_1_carry));  // open: en, clr
endmodule
