// Logisim project fibonacci_2.circ as structural Verilog: 6 circuits, main circuit main
module main (
  input  [31:0] in_1,
  output [31:0] out_2
);

  wire clock_1_out, counter_1_carry;
  wire [31:0] fasv_1_out_2;

  Counter #(.width(6), .max('h3f)) counter_1 (
    .carry(counter_1_carry), .clk(clock_1_out));  // open: load, D, count, Q, clr
  Clock clock_1 (.out(clock_1_out));
  fasv fasv_1 (.in_1(in_1), .out_2(fasv_1_out_2));
  Register #(.width(32)) register_1 (.D(fasv_1_out_2), .Q(out_2), .clk(counter_1_carry));  // open: en, clr
endmodule

module multiply (
  input  [31:0] in_1,
  input  [31:0] in_2,
  input  [31:0] in_3,
  input  [31:0] in_4,
  input  [31:0] in_5,
  input  [31:0] in_6,
  input  [31:0] in_7,
  input  [31:0] in_8,
  output [31:0] out_9,
  output [31:0] out_10,
  output [31:0] out_11,
  output [31:0] out_12
);

  wire [31:0] multiplier_1_out, multiplier_2_out, multiplier_3_out, multiplier_4_out, multiplier_5_out,
       multiplier_6_out, multiplier_7_out, multiplier_8_out;

  Multiplier #(.width(32)) multiplier_1 (.a(in_1), .b(in_5), .out(multiplier_1_out));  // open: cin, cout
  Multiplier #(.width(32)) multiplier_2 (.a(in_2), .b(in_7), .out(multiplier_2_out));  // open: cin, cout
  Multiplier #(.width(32)) multiplier_3 (.a(in_1), .b(in_6), .out(multiplier_3_out));  // open: cin, cout
  Multiplier #(.width(32)) multiplier_4 (.a(in_2), .b(in_8), .out(multiplier_4_out));  // open: cin, cout
  Multiplier #(.width(32)) multiplier_5 (.a(in_3), .b(in_5), .out(multiplier_5_out));  // open: cin, cout
  Multiplier #(.width(32)) multiplier_6 (.a(in_4), .b(in_7), .out(multiplier_6_out));  // open: cin, cout
  Multiplier #(.width(32)) multiplier_7 (.a(in_3), .b(in_6), .out(multiplier_7_out));  // open: cin, cout
  Multiplier #(.width(32)) multiplier_8 (.a(in_4), .b(in_8), .out(multiplier_8_out));  // open: cin, cout
  Adder #(.width(32)) adder_1 (.a(multiplier_1_out), .b(multiplier_2_out), .out(out_9));  // open: cin, cout
  Adder #(.width(32)) adder_2 (.a(multiplier_3_out), .b(multiplier_4_out), .out(out_10));  // open: cin, cout
  Adder #(.width(32)) adder_3 (.a(multiplier_5_out), .b(multiplier_6_out), .out(out_11));  // open: cin, cout
  Adder #(.width(32)) adder_4 (.a(multiplier_7_out), .b(multiplier_8_out), .out(out_12));  // open: cin, cout
endmodule

// Origin
module origin (
  output [31:0] out_1,
  output [31:0] out_2,
  output [31:0] out_3,
  output [31:0] out_4
);


  assign out_1 = 32'h1;
  assign out_2 = 32'h1;
  assign out_3 = 32'h1;
  assign out_4 = {32{1'b0}};
endmodule

module E (
  output [31:0] out_1,
  output [31:0] out_2,
  output [31:0] out_3,
  output [31:0] out_4
);


  assign out_1 = 32'h1;
  assign out_2 = {32{1'b0}};
  assign out_3 = {32{1'b0}};
  assign out_4 = 32'h1;
endmodule

module fasv (
  input  [31:0] in_1,
  output [31:0] out_2
);

  wire clock_1_out, comparator_1_gt, comparator_2_eq, comparator_2_gt, n_left, not_1_out;
  wire [5:0] counter_1_q;
  wire [31:0] e_1_out_1, e_1_out_2, e_1_out_3, e_1_out_4, e_2_out_1, e_2_out_2, e_2_out_3, e_2_out_4,
       multiplexer_1_out, multiplexer_2_out, multiplexer_3_out, multiplexer_4_out, multiplexer_5_out,
       multiplexer_6_out, multiplexer_7_out, multiplexer_8_out, multiply_1_out_9, multiply_1_out_10,
       multiply_1_out_11, multiply_1_out_12, origin_1_out_1, origin_1_out_2, origin_1_out_3, origin_1_out_4,
       s11, s21, s22, self__2_1_out_5, self__2_1_out_6, self__2_1_out_7, self__2_1_out_8;

  Clock clock_1 (.out(clock_1_out));
  E e_1 (.out_1(e_1_out_1), .out_2(e_1_out_2), .out_3(e_1_out_3), .out_4(e_1_out_4));
  Counter #(.width(6), .max('h3f)) counter_1 (.Q(counter_1_q), .clk(clock_1_out));  // open: load, D, count, carry, clr
  Comparator #(.width(6), .mode("unsigned")) comparator_1 (
    .a(counter_1_q), .b(6'b100000), .gt(comparator_1_gt));  // open: eq, lt
  not not_1 (not_1_out, comparator_1_gt);
  Multiplexer #(.width(32)) multiplexer_1 (
    .in0(e_1_out_1), .in1(s11), .out(multiplexer_1_out), .sel(comparator_2_gt));  // open: en
  Multiplexer #(.width(32)) multiplexer_2 (
    .in0(e_1_out_2), .in1(out_2), .out(multiplexer_2_out), .sel(comparator_2_gt));  // open: en
  Multiplexer #(.width(32)) multiplexer_3 (
    .in0(e_1_out_3), .in1(s21), .out(multiplexer_3_out), .sel(comparator_2_gt));  // open: en
  Multiplexer #(.width(32)) multiplexer_4 (
    .in0(e_1_out_4), .in1(s22), .out(multiplexer_4_out), .sel(comparator_2_gt));  // open: en
  Comparator #(.width(6), .mode("unsigned")) comparator_2 (
    .a(counter_1_q), .b({6{1'b0}}), .gt(comparator_2_gt), .eq(comparator_2_eq));  // open: lt
  Shift_Register #(.length(32)) shift_register_1 (
    .in(1'b0), .clk(clock_1_out), .out(n_left), .load(comparator_2_eq), .d0(in_1[0]), .d1(in_1[1]),
    .d2(in_1[2]), .d3(in_1[3]), .d4(in_1[4]), .d5(in_1[5]), .d6(in_1[6]), .d7(in_1[7]), .d8(in_1[8]),
    .d9(in_1[9]), .d10(in_1[10]), .d11(in_1[11]), .d12(in_1[12]), .d13(in_1[13]), .d14(in_1[14]),
    .d15(in_1[15]), .d16(in_1[16]), .d17(in_1[17]), .d18(in_1[18]), .d19(in_1[19]), .d20(in_1[20]),
    .d21(in_1[21]), .d22(in_1[22]), .d23(in_1[23]), .d24(in_1[24]), .d25(in_1[25]), .d26(in_1[26]),
    .d27(in_1[27]), .d28(in_1[28]), .d29(in_1[29]), .d30(in_1[30]), .d31(in_1[31]));  // open: shift, clr, q0, q1, q2, q3, q4, q5, q6, q7, q8, q9, q10, q11, q12, q13, q14, q15, q16, q17, q18, q19, q20, q21, q22, q23, q24, q25, q26, q27, q28, q29, q30, q31
  E e_2 (.out_1(e_2_out_1), .out_2(e_2_out_2), .out_3(e_2_out_3), .out_4(e_2_out_4));
  origin origin_1 (.out_1(origin_1_out_1), .out_2(origin_1_out_2), .out_3(origin_1_out_3), .out_4(origin_1_out_4));
  self__2 self__2_1 (
    .in_1(multiplexer_1_out), .in_2(multiplexer_2_out), .in_3(multiplexer_3_out), .in_4(multiplexer_4_out),
    .out_5(self__2_1_out_5), .out_6(self__2_1_out_6), .out_7(self__2_1_out_7), .out_8(self__2_1_out_8));
  Multiplexer #(.width(32)) multiplexer_5 (
    .in0(e_2_out_1), .in1(origin_1_out_1), .out(multiplexer_5_out), .sel(n_left));  // open: en
  Multiplexer #(.width(32)) multiplexer_6 (
    .in0(e_2_out_2), .in1(origin_1_out_2), .out(multiplexer_6_out), .sel(n_left));  // open: en
  Multiplexer #(.width(32)) multiplexer_7 (
    .in0(e_2_out_3), .in1(origin_1_out_3), .out(multiplexer_7_out), .sel(n_left));  // open: en
  Multiplexer #(.width(32)) multiplexer_8 (
    .in0(e_2_out_4), .in1(origin_1_out_4), .out(multiplexer_8_out), .sel(n_left));  // open: en
  multiply multiply_1 (
    .in_1(self__2_1_out_5), .in_2(self__2_1_out_6), .in_3(self__2_1_out_7), .in_4(self__2_1_out_8),
    .in_5(multiplexer_5_out), .in_6(multiplexer_6_out), .in_7(multiplexer_7_out), .in_8(multiplexer_8_out),
    .out_9(multiply_1_out_9), .out_10(multiply_1_out_10), .out_11(multiply_1_out_11),
    .out_12(multiply_1_out_12));
  Register #(.width(32)) register_1 (.D(multiply_1_out_9), .en(not_1_out), .Q(s11), .clk(clock_1_out));  // open: clr
  Register #(.width(32)) register_2 (.D(multiply_1_out_10), .en(not_1_out), .Q(out_2), .clk(clock_1_out));  // open: clr
  Register #(.width(32)) register_3 (.D(multiply_1_out_11), .en(not_1_out), .Q(s21), .clk(clock_1_out));  // open: clr
  Register #(.width(32)) register_4 (.D(multiply_1_out_12), .en(not_1_out), .Q(s22), .clk(clock_1_out));  // open: clr

  // Other names for the same wires on the sheet: s12[31:0] = out_2
endmodule

module self__2 (
  input  [31:0] in_1,
  input  [31:0] in_2,
  input  [31:0] in_3,
  input  [31:0] in_4,
  output [31:0] out_5,
  output [31:0] out_6,
  output [31:0] out_7,
  output [31:0] out_8
);

  multiply multiply_1 (
    .in_1(in_1), .in_2(in_2), .in_3(in_3), .in_4(in_4), .in_5(in_1), .in_6(in_2), .in_7(in_3), .in_8(in_4),
    .out_9(out_5), .out_10(out_6), .out_11(out_7), .out_12(out_8));
endmodule
