// Logisim project mod5.circ as structural Verilog: 3 circuits, main circuit 状态转移
module \状态转移  (
  input  [1:0] state,
  input  In,
  output [1:0] out_3
);

  wire and_1_out, and_2_out, and_3_out, and_4_out, and_5_out, and_6_out, and_7_out, and_8_out, and_9_out,
       and_10_out, not_1_out, not_2_out, not_3_out, not_4_out, not_5_out, not_6_out, not_7_out, not_8_out,
       or_2_out, or_3_out;

  not not_1 (not_1_out, state[0]);
  not not_2 (not_2_out, state[1]);
  not not_3 (not_3_out, state[0]);
  not not_4 (not_4_out, state[1]);
  not not_5 (not_5_out, state[0]);
  not not_6 (not_6_out, state[1]);
  and and_1 (and_1_out, not_1_out, state[1]);
  or or_1 (out_3[0], and_1_out, and_2_out);
  and and_2 (and_2_out, state[0], not_2_out);
  and and_3 (and_3_out, not_3_out, not_4_out);
  and and_4 (and_4_out, and_3_out, In);
  and and_5 (and_5_out, not_5_out, state[1]);
  and and_6 (and_6_out, and_5_out, not_7_out);
  not not_7 (not_7_out, In);
  and and_7 (and_7_out, state[0], not_6_out);
  and and_8 (and_8_out, and_7_out, not_8_out);
  not not_8 (not_8_out, In);
  and and_9 (and_9_out, state[0], state[1]);
  and and_10 (and_10_out, and_9_out, In);
  or or_2 (or_2_out, and_4_out, and_6_out);
  or or_3 (or_3_out, and_8_out, and_10_out);
  or or_4 (out_3[1], or_2_out, or_3_out);
endmodule

module \状态输出  (
  input  [1:0] in_1,
  input  In,
  output s0,
  output s1,
  output s2,
  output s3,
  output s4
);

  wire and_1_out, and_2_out, and_3_out, and_4_out, and_5_out, and_6_out, and_7_out, and_8_out, and_9_out,
       and_10_out, and_11_out, and_12_out, and_13_out, and_14_out, and_15_out, and_16_out, not_1_out,
       not_2_out, not_3_out, not_4_out, not_5_out, not_6_out, not_7_out, not_8_out, not_9_out, not_10_out,
       not_11_out, not_12_out;

  not not_1 (not_1_out, in_1[0]);
  not not_2 (not_2_out, in_1[1]);
  not not_3 (not_3_out, in_1[0]);
  not not_4 (not_4_out, in_1[1]);
  not not_5 (not_5_out, in_1[0]);
  not not_6 (not_6_out, in_1[1]);
  not not_7 (not_7_out, in_1[0]);
  not not_8 (not_8_out, in_1[1]);
  and and_1 (and_1_out, not_1_out, not_2_out);
  not not_9 (not_9_out, In);
  and and_2 (and_2_out, in_1[0], in_1[1]);
  not not_10 (not_10_out, In);
  and and_3 (and_3_out, not_3_out, not_4_out);
  and and_4 (and_4_out, in_1[0], in_1[1]);
  and and_5 (and_5_out, not_5_out, in_1[1]);
  and and_6 (and_6_out, in_1[0], not_6_out);
  and and_7 (and_7_out, not_7_out, in_1[1]);
  not not_11 (not_11_out, In);
  and and_8 (and_8_out, in_1[0], not_8_out);
  not not_12 (not_12_out, In);
  and and_9 (and_9_out, and_1_out, not_9_out);
  and and_10 (and_10_out, and_2_out, not_10_out);
  and and_11 (and_11_out, and_3_out, In);
  and and_12 (and_12_out, and_4_out, In);
  and and_13 (and_13_out, and_5_out, In);
  and and_14 (and_14_out, and_6_out, In);
  and and_15 (and_15_out, and_7_out, not_11_out);
  and and_16 (and_16_out, and_8_out, not_12_out);
  or or_1 (s1, and_9_out, and_10_out);
  or or_2 (s2, and_11_out, and_12_out);
  or or_3 (s3, and_13_out, and_14_out);
  or or_4 (s4, and_15_out, and_16_out);

  assign s0 = 1'b0;
endmodule

module mod5 (
  input  in_1,
  output out_2,
  output out_3,
  output out_4,
  output out_5,
  output out_6
);

  wire clock_1_out;
  wire [1:0] register_1_q, \状态转移_1_out_3 ;

  \状态转移  \u_状态转移_1  (.state(register_1_q), .In(in_1), .out_3(\状态转移_1_out_3 ));
  Clock clock_1 (.out(clock_1_out));
  Register #(.width(2)) register_1 (.D(\状态转移_1_out_3 ), .Q(register_1_q), .clk(clock_1_out));  // open: en, clr
  \状态输出  \u_状态输出_1  (.in_1(register_1_q), .In(in_1), .s0(out_2), .s1(out_3), .s2(out_4), .s3(out_5), .s4(out_6));
endmodule
